// Logisim project CPU.circ as structural Verilog
// REGS
module REGS16_32 (
  input  [3:0] REG_A_ADDR,
  input  [3:0] REG_B_ADDR,
  input  [3:0] REG_C_ADDR,
  input  [3:0] REG_D_ADDR,
  input  _0_ENA,
  input  CLK,
  input  A_ENA,
  input  A_WE,
  input  [31:0] A_IN,
  input  B_ENA,
  input  B_WE,
  input  [31:0] B_IN,
  input  C_ENA,
  input  C_WE,
  input  [31:0] C_IN,
  input  D_ENA,
  input  D_WE,
  input  [31:0] D_IN,
  output [31:0] A_OUT,
  output [31:0] B_OUT,
  output [31:0] C_OUT,
  output [31:0] D_OUT
);

  wire A_0, A_1, A_2, A_3, A_4, A_5, A_6, A_7, A_8, A_9, A_A, A_B, A_C, A_D, A_E, A_F, and_5_out, and_6_out,
       and_7_out, and_8_out, B_0, B_1, B_2, B_3, B_4, B_5, B_6, B_7, B_8, B_9, B_A, B_B, B_C, B_D, B_E, B_F,
       C_0, C_1, C_2, C_3, C_4, C_5, C_6, C_7, C_8, C_9, C_A, C_B, C_C, C_D, C_E, C_F, D_0, D_1, D_2, D_3,
       D_4, D_5, D_6, D_7, D_8, D_9, D_A, D_B, D_C, D_D, D_E, D_F, or_2_out;
  wire [1:0] or_1_out, pull_resistor_1_node, pull_resistor_2_node, pull_resistor_3_node, pull_resistor_4_node;
  wire [3:0] and_1_out;
  wire [31:0] multiplexer_1_out, register_1_q;

  Decoder #(.select(4), .disabled(0)) decoder_1 (
    .out0(A_0), .out1(A_1), .out2(A_2), .out3(A_3), .out4(A_4), .out5(A_5), .out6(A_6), .out7(A_7),
    .out8(A_8), .out9(A_9), .out10(A_A), .out11(A_B), .out12(A_C), .out13(A_D), .out14(A_E), .out15(A_F),
    .sel(REG_A_ADDR), .en(A_ENA));
  Decoder #(.select(4), .disabled(0)) decoder_2 (
    .out0(B_0), .out1(B_1), .out2(B_2), .out3(B_3), .out4(B_4), .out5(B_5), .out6(B_6), .out7(B_7),
    .out8(B_8), .out9(B_9), .out10(B_A), .out11(B_B), .out12(B_C), .out13(B_D), .out14(B_E), .out15(B_F),
    .sel(REG_B_ADDR), .en(B_ENA));
  Decoder #(.select(4), .disabled(0)) decoder_3 (
    .out0(C_0), .out1(C_1), .out2(C_2), .out3(C_3), .out4(C_4), .out5(C_5), .out6(C_6), .out7(C_7),
    .out8(C_8), .out9(C_9), .out10(C_A), .out11(C_B), .out12(C_C), .out13(C_D), .out14(C_E), .out15(C_F),
    .sel(REG_C_ADDR), .en(C_ENA));
  Decoder #(.select(4), .disabled(0)) decoder_4 (
    .out0(D_0), .out1(D_1), .out2(D_2), .out3(D_3), .out4(D_4), .out5(D_5), .out6(D_6), .out7(D_7),
    .out8(D_8), .out9(D_9), .out10(D_A), .out11(D_B), .out12(D_C), .out13(D_D), .out14(D_E), .out15(D_F),
    .sel(REG_D_ADDR), .en(D_ENA));
  buf and_1 (and_1_out[0], A_0);  // AND_Gate
  buf and_2 (and_1_out[1], B_0);  // AND_Gate
  buf and_3 (and_1_out[2], C_0);  // AND_Gate
  buf and_4 (and_1_out[3], D_0);  // AND_Gate
  Pull_Resistor pull_resistor_1 (.node(pull_resistor_1_node));
  assign pull_resistor_1_node = and_1_out[0] ? 2'b00 : 2'bz;  // Controlled_Buffer controlled_buffer_1
  Pull_Resistor pull_resistor_2 (.node(pull_resistor_2_node));
  assign pull_resistor_2_node = and_1_out[1] ? 2'b01 : 2'bz;  // Controlled_Buffer controlled_buffer_2
  Pull_Resistor pull_resistor_3 (.node(pull_resistor_3_node));
  assign pull_resistor_3_node = and_1_out[2] ? 2'b10 : 2'bz;  // Controlled_Buffer controlled_buffer_3
  Pull_Resistor pull_resistor_4 (.node(pull_resistor_4_node));
  assign pull_resistor_4_node = and_1_out[3] ? 2'b11 : 2'bz;  // Controlled_Buffer controlled_buffer_4
  assign or_1_out = pull_resistor_1_node | pull_resistor_2_node | pull_resistor_3_node | pull_resistor_4_node;  // OR_Gate or_1, 2 bits wide
  Multiplexer #(.select(2), .width(32), .disabled(0), .enable("false")) multiplexer_1 (
    .in0(A_IN), .in1(B_IN), .in2(C_IN), .in3(D_IN), .out(multiplexer_1_out), .sel(or_1_out));
  or or_2 (or_2_out, and_1_out[0], and_1_out[1], and_1_out[2], and_1_out[3]);
  and and_5 (and_5_out, A_0, ~A_WE);  // AND_Gate
  Register #(.width(32)) register_1 (.D(multiplexer_1_out), .en(or_2_out), .Q(register_1_q), .clk(CLK), .clr(_0_ENA));
  assign A_OUT = and_5_out ? register_1_q : 32'bz;  // Controlled_Buffer controlled_buffer_5
  and and_6 (and_6_out, C_0, ~C_WE);  // AND_Gate
  and and_7 (and_7_out, B_0, ~B_WE);  // AND_Gate
  assign C_OUT = and_6_out ? register_1_q : 32'bz;  // Controlled_Buffer controlled_buffer_6
  assign B_OUT = and_7_out ? register_1_q : 32'bz;  // Controlled_Buffer controlled_buffer_7
  and and_8 (and_8_out, D_0, ~D_WE);  // AND_Gate
  assign D_OUT = and_8_out ? register_1_q : 32'bz;  // Controlled_Buffer controlled_buffer_8

  // Notes on the sheet:
  //   REG_C_ADDR: pull=down
  //   REG_D_ADDR: pull=down
  //   C_OUT: pull=down
  //   B_OUT: pull=down
  //   C_ENA: pull=down
  //   REG_B_ADDR: pull=down
  //   B_WE: pull=down
  //   A_WE: pull=down
  //   D_OUT: pull=down
  //   REG_A_ADDR: pull=down
  //   C_WE: pull=down
  //   D_ENA: pull=down
  //   B_ENA: pull=down
  //   CLK: pull=down
  //   D_WE: pull=down
  //   A_ENA: pull=down
  //   A_OUT: pull=down
  //   _0_ENA: pull=down
endmodule

module REGS256_32 (
);

  wire A_ENA, A_WE, B_ENA, B_WE, C_ENA, CLK, Transfer, transmission_1_p3;
  wire [3:0] A_ADR_LO, B_ADR_LO, C_ADR_LO;
  wire [31:0] A_DATA, B_DATA, C_DATA;

  // NOT_Gate not_1 has open pins: in=Transfer, out=open
  // Transmission_Gate #(.width(32)) transmission_1: pin names not known; wires that end beside it: {32{1'b1}}, Transfer, transmission_1_p3
  // Probe on transmission_1_p3
  Button button_1 (.out(Transfer));
  REGS16_32 regs16_32_1 (
    .A_ENA(A_ENA), .A_WE(A_WE), .A_IN(A_DATA), .A_OUT(A_DATA), .B_ENA(B_ENA), .B_WE(B_WE), .B_IN(B_DATA),
    .B_OUT(B_DATA), .C_ENA(C_ENA), .C_WE(A_WE), .C_IN(C_DATA), .C_OUT(C_DATA), .REG_A_ADDR(A_ADR_LO),
    .REG_B_ADDR(B_ADR_LO), .REG_C_ADDR(C_ADR_LO), .CLK(CLK), .D_ENA(CLK));  // open: REG_D_ADDR, D_WE, D_IN, D_OUT, _0_ENA
endmodule

module INTERRUPT_STACK (
  input  POP,
  input  PUSH,
  input  ENA,
  input  [31:0] DATA_IN,
  output [31:0] DATA_OUT
);

  wire _1, _2, _3, _CLK, buffer_3_out, button_1_out, CLK, DEC, INC, not_2_out, or_1_out, WE;
  wire [0:0] decoder_1_out0;
  wire [7:0] counter_1_q;
  wire [31:0] pull_resistor_3_node, ram_1_data;

  Pull_Resistor pull_resistor_1 (.node(DEC));
  or or_1 (or_1_out, DEC, INC);
  Button button_1 (.out(button_1_out));
  Pull_Resistor pull_resistor_2 (.node(or_1_out));
  Decoder #(.select(2)) decoder_1 (
    .out0(decoder_1_out0[0]), .out1(_1), .out2(_2), .out3(_3), .sel({PUSH, POP}), .en(ENA));
  not not_1 (_CLK, CLK);
  Clock clock_1 (.out(CLK));
  Counter #(.ongoal("stay"), .trigger("falling")) counter_1 (
    .load(DEC), .count(or_1_out), .Q(counter_1_q), .clk(_CLK), .clr(button_1_out));  // open: D, carry
  Pull_Resistor pull_resistor_3 (.node(pull_resistor_3_node));
  assign pull_resistor_3_node = WE ? DATA_IN : 32'bz;  // Controlled_Buffer controlled_buffer_1
  buf buffer_1 (DEC, _1);
  Pull_Resistor pull_resistor_4 (.node(_1));
  buf buffer_2 (INC, _2);
  Pull_Resistor pull_resistor_5 (.node(_2));
  buf buffer_3 (buffer_3_out, _3);
  Pull_Resistor pull_resistor_6 (.node(_3));
  not not_2 (not_2_out, WE);
  assign DATA_OUT = not_2_out ? ram_1_data : 32'bz;  // Controlled_Buffer controlled_buffer_2
  RAM #(.dataWidth(32), .bus("separate")) ram_1 (
    .addr(counter_1_q), .din(pull_resistor_3_node), .data(ram_1_data), .str(WE), .sel(ENA), .clk(CLK));  // open: ld, clr
  or or_2 (WE, _2, buffer_3_out);

  // Notes on the sheet:
  //   POP: pull=down
  //   PUSH: pull=down
  //   DATA_OUT: pull=down
  //   DATA_IN: pull=down
  //   ENA: pull=down
endmodule
